# Fritzing sketch PIR schema (fritzing) (saved by Fritzing 0.9.3b)
breadboards: 1

parts:
  PIR = PIR sensor
  R1 = Resistor [tolerance=±5% resistance=220 package=THT]
  LED1 = LED - 5mm [color="Red (633nm)" package="5 mm [THT]"]

nets:
  3.3V: PIR.VDD
  G15 / Pxx: PIR.SIG, R1.Pin_1
  GND: PIR.GND, LED1.cathode
  N1: R1.Pin_0, LED1.anode

notes:
  GND
  G15 / Pxx
  3V
  Vcc
  OUT
  PIR sensor
  naar Expansionboard GND
  naar Expansionboard
  LED is optioneel
  202-0403 PP
